# Fritzing sketch Rangkaian Schematic (saved by Fritzing 0.9.3b)
breadboards: 1

parts:
  U1 = ESP32S-HiLetgo [part_number=ESP32S-HiLetgo]
  A1 = 2 channel relay module [package=THT]
  WATER_PUMP1 = water pump/motor  # not connected
  VALVE1 = Plastic Solenoid Valve
  JACK1 = 2.1mm Barrel Jack with Terminal Block
  JACK2 = 2.1mm Barrel Jack with Terminal Block  # not connected
  IR_Sensor_Switch1 = Infrared Sensor Switch

nets:
  N1: U1.GPIO35, IR_Sensor_Switch1.GND
  N2: U1.GPIO26, A1.pin_16
  VIN: U1.VIN, A1.pin_14, IR_Sensor_Switch1.Vcc
  N3: U1.GND, A1.pin_13, IR_Sensor_Switch1.OUT
  N4: A1.pin_2, JACK1.NEG
  N5: VALVE1.no_name_yet#1, JACK1.POS

custom parts:
  ESP32S-HiLetgo: HiLetgo ESP-WROOM-32 ESP32 ESP-32S Development Board 2.4GHz Dual-Mode WiFi + Bluetooth Dual Cores Microcontroller The ESP32 integrated with Antenna switches, RF Balun, power amplifiers, low-noise amplifiers, filters, and management modules, and the entire solution occupies the least area of PCB. 2.4 GHz Wi-Fi plus Bluetooth dual-mode chip, with TSMC Ultra-low power consumption 40nm technology,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
  2 channel relay module: 2 channel Relay Module 5V 12V 24V High and Low Level Trigger Relay Control With Optocoupler Two Way relays DC 5 V 12 V 24 V Volt.
  water pump/motor: WATER PUMP BY ARDUBLOCKTR
  Infrared Sensor Switch: - Working voltage: DC 5V - Working current: 10~15mA - Detecting range: 3~80cm (adjustable) - Red: VCC, Green: GND, Yellow: OUT
